// Logisim project absolute.circ as structural Verilog: 1 circuit, main circuit main
module main (
  input  I_3,
  input  I_2,
  input  I_1,
  input  I_0,
  output O_2,
  output O_1,
  output O_0
);

  wire and_1_out, and_2_out, and_3_out, and_4_out, and_5_out, and_6_out, not_1_out, not_2_out, not_3_out,
       not_4_out;

  not not_1 (not_1_out, I_3);
  not not_2 (not_2_out, I_2);
  not not_3 (not_3_out, I_1);
  not not_4 (not_4_out, I_0);
  and and_1 (and_1_out, not_1_out, I_2);
  and and_2 (and_2_out, I_3, not_2_out);
  and and_3 (and_3_out, I_2, not_3_out, not_4_out);
  or or_1 (O_2, and_1_out, and_2_out, and_3_out);
  and and_4 (and_4_out, not_1_out, I_1);
  and and_5 (and_5_out, I_1, not_4_out);
  and and_6 (and_6_out, I_3, not_3_out, I_0);
  or or_2 (O_1, and_4_out, and_5_out, and_6_out);

  assign O_0 = I_0;
endmodule
