// Logisim project adder.circ as structural Verilog: 1 circuit, main circuit main
module main (
  input  B_3,
  input  A_3,
  input  B_2,
  input  A_2,
  input  B_1,
  input  A_1,
  input  B_0,
  input  A_0,
  output Cout,
  output O_3,
  output O_2,
  output O_1,
  output O_0
);

  wire main_2_cout, main_3_cout, main_4_cout;

  full_adder_main main_1 (.A(A_3), .B(B_3), .Cin(main_2_cout), .SUM(O_3), .Cout(Cout));
  full_adder_main main_2 (.A(A_2), .B(B_2), .Cin(main_3_cout), .SUM(O_2), .Cout(main_2_cout));
  full_adder_main main_3 (.A(A_1), .B(B_1), .Cin(main_4_cout), .SUM(O_1), .Cout(main_3_cout));
  full_adder_main main_4 (.A(A_0), .B(B_0), .Cin(1'b0), .SUM(O_0), .Cout(main_4_cout));
endmodule
