// Logisim project decoder.circ as structural Verilog: 1 circuit, main circuit main
module main (
  input  I_2,
  input  I_1,
  input  I_0,
  output A,
  output B,
  output C,
  output D,
  output E,
  output F,
  output G
);

  wire and_1_out, and_2_out, and_3_out, and_4_out, and_5_out, and_6_out, and_7_out, and_8_out, and_9_out,
       not_1_out, not_2_out, not_3_out;

  not not_1 (not_1_out, I_2);
  not not_2 (not_2_out, I_1);
  not not_3 (not_3_out, I_0);
  and and_1 (and_1_out, I_2, I_0);
  and and_2 (and_2_out, not_1_out, not_3_out);
  and and_3 (and_3_out, I_1, I_0);
  and and_4 (and_4_out, not_2_out, not_3_out);
  and and_5 (and_5_out, I_1, not_3_out);
  and and_6 (and_6_out, not_1_out, I_1);
  and and_7 (and_7_out, I_2, not_2_out, I_0);
  and and_8 (and_8_out, I_2, not_2_out);
  and and_9 (and_9_out, I_2, not_3_out);
  or or_1 (A, and_1_out, I_1, and_2_out);
  or or_2 (B, and_3_out, not_1_out, and_4_out);
  or or_3 (C, I_2, not_2_out, I_0);
  or or_4 (D, and_2_out, and_5_out, and_6_out, and_7_out);
  or or_5 (E, and_5_out, and_2_out);
  or or_6 (F, and_4_out, and_9_out, and_8_out);
  or or_7 (G, and_5_out, and_6_out, and_8_out);
endmodule
