// Logisim project full_adder.circ as structural Verilog: 1 circuit, main circuit main
module main (
  input  Cin,
  input  A,
  input  B,
  output SUM,
  output Cout
);

  wire main_1_cout, main_1_o, main_2_cout;

  half_adder_main main_1 (.A(A), .B(B), .O(main_1_o), .COUT(main_1_cout));
  half_adder_main main_2 (.A(Cin), .B(main_1_o), .O(SUM), .COUT(main_2_cout));
  or or_1 (Cout, main_2_cout, main_1_cout);
endmodule
