// Logisim project half_adder.circ as structural Verilog: 1 circuit, main circuit main
module main (
  input  A,
  input  B,
  output O,
  output COUT
);

  xor xor_1 (O, A, B);
  and and_1 (COUT, A, B);
endmodule
