// Logisim project work01.circ as structural Verilog: 1 circuit, main circuit main
module main (
  input  A_3,
  input  A_2,
  input  A_1,
  input  A_0,
  input  B_3,
  input  B_2,
  input  B_1,
  input  B_0
);

  wire main_1_o_0, main_1_o_1, main_1_o_2, main_1_o_3, main_2_o_0, main_2_o_1, main_2_o_2, main_2_o_3,
       main_3_o_0, main_3_o_1, main_3_o_2, main_3_o_3, main_4_o_0, main_4_o_1, main_4_o_2, main_4_o_3,
       main_5_o_0, main_5_o_1, main_5_o_2, main_6_o_0, main_6_o_1, main_6_o_2, main_7_o_0, main_7_o_1,
       main_7_o_2, main_8_o_0, main_8_o_1, main_8_o_2, main_9_a, main_9_b, main_9_c, main_9_d, main_9_e,
       main_9_f, main_9_g, main_10_a, main_10_b, main_10_c, main_10_d, main_10_e, main_10_f, main_10_g,
       main_11_a, main_11_b, main_11_c, main_11_d, main_11_e, main_11_f, main_11_g, main_12_a, main_12_b,
       main_12_c, main_12_d, main_12_e, main_12_f, main_12_g, not_1_out, not_2_out, transistor_1_out,
       transistor_2_out, transistor_3_out, transistor_4_out, transistor_5_out, transistor_6_out,
       transistor_7_out, transistor_8_out, transistor_9_out, transistor_10_out, transistor_11_out,
       transistor_12_out, transistor_13_out, transistor_14_out, transistor_15_out, transistor_16_out,
       transistor_17_out, transistor_18_out, transistor_19_out, transistor_20_out, transistor_21_out,
       transistor_22_out, transistor_23_out, transistor_24_out, transistor_25_out, transistor_26_out,
       transistor_27_out, transistor_28_out;

  adder_main main_1 (
    .B_3(A_3), .A_3(1'b1), .B_2(A_2), .A_2(1'b1), .B_1(A_1), .A_1(1'b1), .B_0(A_0), .A_0(1'b1),
    .O_3(main_1_o_3), .O_2(main_1_o_2), .O_1(main_1_o_1), .O_0(main_1_o_0));  // open: Cout
  adder_main main_2 (
    .B_3(A_3), .A_3(1'b0), .B_2(A_2), .A_2(1'b0), .B_1(A_1), .A_1(1'b0), .B_0(A_0), .A_0(1'b1),
    .O_3(main_2_o_3), .O_2(main_2_o_2), .O_1(main_2_o_1), .O_0(main_2_o_0));  // open: Cout
  adder_main main_3 (
    .B_3(B_3), .A_3(1'b1), .B_2(B_2), .A_2(1'b1), .B_1(B_1), .A_1(1'b1), .B_0(B_0), .A_0(1'b1),
    .O_3(main_3_o_3), .O_2(main_3_o_2), .O_1(main_3_o_1), .O_0(main_3_o_0));  // open: Cout
  adder_main main_4 (
    .B_3(B_3), .A_3(1'b0), .B_2(B_2), .A_2(1'b0), .B_1(B_1), .A_1(1'b0), .B_0(B_0), .A_0(1'b1),
    .O_3(main_4_o_3), .O_2(main_4_o_2), .O_1(main_4_o_1), .O_0(main_4_o_0));  // open: Cout
  absolute_main main_5 (
    .O_2(main_5_o_2), .O_1(main_5_o_1), .O_0(main_5_o_0), .I_3(main_1_o_3), .I_2(main_1_o_2),
    .I_1(main_1_o_1), .I_0(main_1_o_0));
  absolute_main main_6 (
    .O_2(main_6_o_2), .O_1(main_6_o_1), .O_0(main_6_o_0), .I_3(main_2_o_3), .I_2(main_2_o_2),
    .I_1(main_2_o_1), .I_0(main_2_o_0));
  absolute_main main_7 (
    .O_2(main_7_o_2), .O_1(main_7_o_1), .O_0(main_7_o_0), .I_3(main_3_o_3), .I_2(main_3_o_2),
    .I_1(main_3_o_1), .I_0(main_3_o_0));
  absolute_main main_8 (
    .O_2(main_8_o_2), .O_1(main_8_o_1), .O_0(main_8_o_0), .I_3(main_4_o_3), .I_2(main_4_o_2),
    .I_1(main_4_o_1), .I_0(main_4_o_0));
  decoder_main main_9 (
    .A(main_9_a), .B(main_9_b), .C(main_9_c), .D(main_9_d), .E(main_9_e), .F(main_9_f), .G(main_9_g),
    .I_2(main_5_o_2), .I_1(main_5_o_1), .I_0(main_5_o_0));
  not not_1 (not_1_out, A_3);
  decoder_main main_10 (
    .A(main_10_a), .B(main_10_b), .C(main_10_c), .D(main_10_d), .E(main_10_e), .F(main_10_f), .G(main_10_g),
    .I_2(main_6_o_2), .I_1(main_6_o_1), .I_0(main_6_o_0));
  decoder_main main_11 (
    .A(main_11_a), .B(main_11_b), .C(main_11_c), .D(main_11_d), .E(main_11_e), .F(main_11_f), .G(main_11_g),
    .I_2(main_7_o_2), .I_1(main_7_o_1), .I_0(main_7_o_0));
  not not_2 (not_2_out, B_3);
  decoder_main main_12 (
    .A(main_12_a), .B(main_12_b), .C(main_12_c), .D(main_12_d), .E(main_12_e), .F(main_12_f), .G(main_12_g),
    .I_2(main_8_o_2), .I_1(main_8_o_1), .I_0(main_8_o_0));
  Transistor #(.gate("br")) transistor_1 (.in(main_9_a), .out(transistor_1_out), .gate(A_3));
  Transistor transistor_2 (.in(main_10_a), .out(transistor_2_out), .gate(not_1_out));
  Transistor #(.gate("br")) transistor_3 (.in(main_11_a), .out(transistor_3_out), .gate(B_3));
  Transistor transistor_4 (.in(main_12_a), .out(transistor_4_out), .gate(not_2_out));
  Transistor #(.gate("br")) transistor_5 (.in(main_9_b), .out(transistor_5_out), .gate(A_3));
  Transistor #(.gate("br")) transistor_6 (.in(main_9_c), .out(transistor_6_out), .gate(A_3));
  Transistor transistor_7 (.in(main_10_b), .out(transistor_7_out), .gate(not_1_out));
  Transistor transistor_8 (.in(main_10_c), .out(transistor_8_out), .gate(not_1_out));
  Transistor #(.gate("br")) transistor_9 (.in(main_11_b), .out(transistor_9_out), .gate(B_3));
  Transistor #(.gate("br")) transistor_10 (.in(main_11_c), .out(transistor_10_out), .gate(B_3));
  Transistor transistor_11 (.in(main_12_b), .out(transistor_11_out), .gate(not_2_out));
  Transistor transistor_12 (.in(main_12_c), .out(transistor_12_out), .gate(not_2_out));
  Transistor #(.gate("br")) transistor_13 (.in(main_9_d), .out(transistor_13_out), .gate(A_3));
  Transistor transistor_14 (.in(main_10_d), .out(transistor_14_out), .gate(not_1_out));
  Transistor transistor_15 (.in(main_10_e), .out(transistor_15_out), .gate(not_1_out));
  Transistor #(.gate("br")) transistor_16 (.in(main_11_d), .out(transistor_16_out), .gate(B_3));
  Transistor transistor_17 (.in(main_12_d), .out(transistor_17_out), .gate(not_2_out));
  Transistor transistor_18 (.in(main_12_e), .out(transistor_18_out), .gate(not_2_out));
  _7_Segment_Display u_7_segment_display_1 (
    .g(transistor_25_out), .f(transistor_20_out), .a(transistor_1_out), .b(transistor_5_out),
    .e(transistor_19_out), .d(transistor_13_out), .c(transistor_6_out));  // open: dp
  Transistor #(.gate("br")) transistor_19 (.in(main_9_e), .out(transistor_19_out), .gate(A_3));
  Transistor #(.gate("br")) transistor_20 (.in(main_9_f), .out(transistor_20_out), .gate(A_3));
  _7_Segment_Display u_7_segment_display_2 (
    .g(transistor_27_out), .f(transistor_21_out), .a(transistor_2_out), .b(transistor_7_out),
    .e(transistor_15_out), .d(transistor_14_out), .c(transistor_8_out));  // open: dp
  Transistor transistor_21 (.in(main_10_f), .out(transistor_21_out), .gate(not_1_out));
  Transistor #(.gate("br")) transistor_22 (.in(main_11_e), .out(transistor_22_out), .gate(B_3));
  Transistor #(.gate("br")) transistor_23 (.in(main_11_f), .out(transistor_23_out), .gate(B_3));
  _7_Segment_Display u_7_segment_display_3 (
    .g(transistor_28_out), .f(transistor_24_out), .a(transistor_4_out), .b(transistor_11_out),
    .e(transistor_18_out), .d(transistor_17_out), .c(transistor_12_out));  // open: dp
  Transistor transistor_24 (.in(main_12_f), .out(transistor_24_out), .gate(not_2_out));
  Transistor #(.gate("br")) transistor_25 (.in(main_9_g), .out(transistor_25_out), .gate(A_3));
  _7_Segment_Display u_7_segment_display_4 (
    .g(transistor_26_out), .f(transistor_23_out), .a(transistor_3_out), .b(transistor_9_out),
    .e(transistor_22_out), .d(transistor_16_out), .c(transistor_10_out));  // open: dp
  Transistor #(.gate("br")) transistor_26 (.in(main_11_g), .out(transistor_26_out), .gate(B_3));
  Transistor transistor_27 (.in(main_10_g), .out(transistor_27_out), .gate(not_1_out));
  Transistor transistor_28 (.in(main_12_g), .out(transistor_28_out), .gate(not_2_out));
endmodule
